# Fritzing sketch Weather_Station (saved by Fritzing 0.9.3b)
breadboards: 1

parts:
  DHT1 = DHT22 Humidity and Temperature Sensor
  SparkFun_ESP8266_Thing_-_Dev_Board1 = SparkFun ESP8266 Thing - Dev Board [part_number=WRL-13711]
  Part1 = Adafruit 1.54" Tri-Color eInk / ePaper Display with SRAM [part_number=3625]
  Part2 = Arduino Pro Mini v13
  R1 = Resistor [tolerance=±5% resistance=10k package=THT]
  Part3 = Adafruit BME280
  SparkFun_ESP8266_Thing_-_Dev_Board2 = SparkFun ESP8266 Thing - Dev Board [part_number=WRL-13711]
  Part4 = Adafruit 1.54" Tri-Color eInk / ePaper Display with SRAM [part_number=3625]

nets:
  5V: DHT1.VDD, SparkFun_ESP8266_Thing_-_Dev_Board1.VIN, R1.Pin_0, SparkFun_ESP8266_Thing_-_Dev_Board2.VIN
  N1: DHT1.DATA, SparkFun_ESP8266_Thing_-_Dev_Board1.9, R1.Pin_1
  GND: DHT1.GND, SparkFun_ESP8266_Thing_-_Dev_Board1.GND, Part1.GND, Part2.GND, Part3.GND, SparkFun_ESP8266_Thing_-_Dev_Board2.GND, Part4.GND
  N2: SparkFun_ESP8266_Thing_-_Dev_Board1.VCC, Part2.RAW
  N3: SparkFun_ESP8266_Thing_-_Dev_Board1.U0TXO, Part2.D1/RX
  N4: SparkFun_ESP8266_Thing_-_Dev_Board1.U0RXI, Part2.D0/TX
  VIN: Part1.VIN, Part2.VCC
  N5: Part1.SCLK, Part2.D13/SCK
  N6: Part1.MISO, Part2.D12/MISO
  N7: Part1.MOSI, Part2.D11_PWM/MOSI
  N8: Part1.DISPCS, Part2.D6_PWM
  N9: Part1.DC, Part2.D10_PWM/SS
  N10: Part1.SRAMCS, Part2.D9_PWM
  N11: Part1.SDCS, Part2.D8
  N12: Part1.RESET, Part2.RESET
  VIN_2: Part3.VIN, SparkFun_ESP8266_Thing_-_Dev_Board2.VCC
  N13: Part3.SCK/SCL, SparkFun_ESP8266_Thing_-_Dev_Board2.GPIO15
  N14: Part3.SDI/SDA, SparkFun_ESP8266_Thing_-_Dev_Board2.GPIO2
  N15: SparkFun_ESP8266_Thing_-_Dev_Board2.GPIO14, Part4.SCLK
  N16: SparkFun_ESP8266_Thing_-_Dev_Board2.RESET, Part4.RESET
  N17: SparkFun_ESP8266_Thing_-_Dev_Board2.USBVCC, Part4.VIN
  N18: SparkFun_ESP8266_Thing_-_Dev_Board2.9, Part4.DC
  N19: SparkFun_ESP8266_Thing_-_Dev_Board2.GPIO5, Part4.DISPCS
  N20: SparkFun_ESP8266_Thing_-_Dev_Board2.GPIO4, Part4.SRAMCS
  N21: SparkFun_ESP8266_Thing_-_Dev_Board2.GPIO13, Part4.MOSI
  N22: SparkFun_ESP8266_Thing_-_Dev_Board2.GPIO12, Part4.MISO
  N23: SparkFun_ESP8266_Thing_-_Dev_Board2.GPIO16, Part4.SDCS

notes:
  DISPCS == ECS

custom parts:
  SparkFun ESP8266 Thing - Dev Board: This is the SparkFun ESP8266 Thing Dev Board – a development board that has been solely designed around the ESP8266, with an integrated FTDI USB-to-Serial chip. The ESP8266 is a cost-effective, and very capable WiFi-enabled microcontroller. Like any microcontroller, it can be programmed to blink LEDs, trigger relays, monitor sensors, or automate coffee makers, and with an integrated WiFi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
  Adafruit 1.54" Tri-Color eInk / ePaper Display with SRAM: This small 1.54" tri-color display has 152x152 black and red ink pixels and a white-ish background. Using our Arduino library, you can create a 'frame buffer' with what pixels you want to have activated and then write that out to the display. We tossed a small SRAM chip on the back. This chip shares the SPI port the eInk display uses, so you only need one extra pin. And, no more frame-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
  Adafruit BME280: Bosch has stepped up their game with their new BME280 sensor, an environmental sensor with temperature, barometric pressure and humidity! This sensor is great for all sorts of weather/environmental sensing and can even be used in both I2C and SPI! This precision sensor from Bosch is the best low-cost sensing solution for measuring humidity with ±3% accuracy, barometric pressure with ±1 hPa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
